// Logisim project AE_02_2025.circ as structural Verilog: 1 circuit, main circuit main
module main (
  input  En_PC,
  input  [1:0] Sel_0,
  input  [1:0] Sel_1,
  input  Sel_2,
  output [3:0] Output,
  output Op_FSM
);

  wire clock_1_out;
  wire [3:0] counter_1_q, multiplexer_1_out, multiplexer_2_out, multiplier_1_out, Reg_MULT_q, Reg_SUB_q,
       subtractor_1_out;
  wire [7:0] ram_1_data;

  Clock clock_1 (.out(clock_1_out));
  Counter #(.width(4), .max('hf)) counter_1 (
    .count(En_PC), .Q(counter_1_q), .clk(clock_1_out));  // open: load, D, carry, clr
  RAM #(.addrWidth(4), .dataWidth(9)) ram_1 (
    .addr(counter_1_q), .data({Op_FSM, ram_1_data}));  // open: sel, clk, ld, clr
  Multiplexer #(.select(2), .width(4), .enable("false")) multiplexer_1 (
    .in0(ram_1_data[3:0]), .in1(ram_1_data[7:4]), .in2(Reg_MULT_q), .in3(Reg_SUB_q), .out(multiplexer_1_out),
    .sel(Sel_0));
  Multiplexer #(.select(2), .width(4), .enable("false")) multiplexer_2 (
    .in0(ram_1_data[3:0]), .in1(ram_1_data[7:4]), .in2(Reg_MULT_q), .in3(Reg_SUB_q), .out(multiplexer_2_out),
    .sel(Sel_1));
  Multiplier #(.width(4)) multiplier_1 (
    .a(multiplexer_1_out), .b(multiplexer_2_out), .out(multiplier_1_out));  // open: cin, cout
  Subtractor #(.width(4)) subtractor_1 (
    .a(multiplexer_1_out), .b(multiplexer_2_out), .out(subtractor_1_out));  // open: bin, bout
  Register #(.width(4)) Reg_MULT (.D(multiplier_1_out), .Q(Reg_MULT_q), .clk(clock_1_out));  // open: en, clr
  Register #(.width(4)) Reg_SUB (.D(subtractor_1_out), .Q(Reg_SUB_q), .clk(clock_1_out));  // open: en, clr
  Multiplexer #(.width(4), .enable("false")) multiplexer_3 (
    .in0(Reg_MULT_q), .in1(Reg_SUB_q), .out(Output), .sel(Sel_2));

  // Notes on the sheet:
  //   OP_FSM,A,B
  //   b
endmodule
